# Fritzing sketch wiring (saved by Fritzing 0.9.3b)

parts:
  Part1 = Arduino Nano (Rev3.0)
  R1 = Resistor [tolerance=±5% resistance=220 package=THT]
  LED-R = LED - 3mm [color="Red (633nm)" package="3 mm [THT]"]
  R2 = Resistor [tolerance=±5% resistance=220 package=THT]
  LED-S = LED - 3mm [color="Red (633nm)" package="3 mm [THT]"]
  SW-S = Pushbutton [package="[SMD]"]
  SW-R = Pushbutton [package="[SMD]"]
  NRF24L1 = NRF24L01
  C1 = Ceramic Capacitor [capacitance=10nF package="0805 [SMD, multilayer]"]
  C2 = Electrolytic Capacitor [capacitance=1000µF package="300 mil [THT, electrolytic]"]
  SW-RST = Pushbutton [package="[SMD]"]
  SSR = RELAY-SOLIDSTATE [package=relay-s108t02]
  J1a = female pin header, 8 pins [form="♀ (female)"]
  J1b = female pin header, 8 pins [form="♀ (female)"]
  F1 = FUSE [package=fuse_5mm]
  J-S1 = female pin header, 3 pins [form="♀ (female)"]
  J-S2 = female pin header, 3 pins [form="♀ (female)"]
  J-S3 = female pin header, 3 pins [form="♀ (female)"]
  J-SSR-1 = female pin header, 2 pins [form="♀ (female)"]
  J-PSU-5 = female pin header, 2 pins [form="♀ (female)"]
  J220-In = Camdenboss CTB0158-2 [part_number=. package=THT]
  J220-Out = Camdenboss CTB0158-2 [part_number=. package=THT]
  J-Earth = Camdenboss CTB0158-2 [part_number=. package=THT]
  P1 = Rotary Potentiometer (Small) [maximum_resistance=10kΩ package=THT]
  R5 = Resistor [tolerance=±5% resistance=330 package=THT]
  J220-Sw = Camdenboss CTB0158-2 [part_number=. package=THT]
  J220-Fuse = Camdenboss CTB0158-2 [part_number=. package=THT]
  SW-220 = Taiway 100-SP-X-T1 SPDT Miniature Toggle Switch [part_number=. package=THT]
  J220-SSR- = Camdenboss CTB0158-2 [part_number=. package=THT]
  J-PSU-220 = Main Connector [part_number=. package=THT]

nets:
  GND: Part1.RESET, Part1.GND, LED-R.cathode, LED-S.cathode, SW-S.Pin_3, SW-S.Pin_4, SW-R.Pin_3, SW-R.Pin_4, NRF24L1.GND, C1.0, C2.-, SW-RST.Pin_1, SSR.-, J1a.pin1, J1a.pin2, J1b.pin2, J-S1.pin1, J-S2.pin1, J-S3.pin1, J-SSR-1.pin1, J-PSU-5.pin2, P1.leg1
  N1: Part1.D5, R1.Pin_1
  N2: Part1.D6, R2.Pin_1
  N3: Part1.D7, J1a.pin5
  N4: Part1.D8, J1a.pin6
  N5: Part1.D9, NRF24L1.CE
  N6: Part1.D10, NRF24L1.CSN
  N7: Part1.D11/MOSI, NRF24L1.MOSI
  N8: Part1.D12/MISO, NRF24L1.MISO
  5V: Part1.5V, C2.+, J1a.pin8, J-S1.pin3, J-S2.pin3, J-S3.pin3, J-PSU-5.pin1
  N9: Part1.A3, R5.Pin_1
  N10: Part1.A2, SSR.+, J-SSR-1.pin2
  N11: Part1.A0, C1.1, J1a.pin7
  3V3: Part1.3V3, NRF24L1.VCC
  N12: Part1.D13/SCK, NRF24L1.SCK
  N13: R1.Pin_0, J1a.pin3
  N14: LED-R.anode, J1b.pin4
  N15: R2.Pin_0, J1a.pin4
  N16: LED-S.anode, J1b.pin3
  N17: SW-S.Pin_1, SW-S.Pin_2, J1b.pin6
  N18: SW-R.Pin_1, SW-R.Pin_2, J1b.pin5
  N19: SW-RST.Pin_3, J1b.pin1
  N20: SSR.T1, J220-SSR-.terminal_1
  N21: SSR.T2, J220-SSR-.terminal_2
  N22: J1b.pin7, P1.wiper
  N23: J1b.pin8, P1.leg2
  N24: F1.1, J220-Fuse.terminal_2
  N25: F1.2, J220-Fuse.terminal_1
  N26: J-S1.pin2, J-S2.pin2, J-S3.pin2, R5.Pin_0
  N27: J220-In.pin1, J220-Sw.pin2
  N28: J220-In.pin2, J220-Out.pin1, J-PSU-220.pinN
  N29: J220-Out.pin2, J220-SSR-.pin1
  N30: J-Earth.pin1, J-Earth.pin2, J-PSU-220.pinP
  N31: J220-Sw.pin1, J220-Fuse.pin2
  N32: J220-Sw.terminal_1, SW-220.COM
  N33: J220-Sw.terminal_2, SW-220.L2
  N34: J220-Fuse.pin1, J220-SSR-.pin2, J-PSU-220.pinT

custom parts:
  NRF24L01: NRF24L01 module
  Main Connector: Camdenboss CTB0158-3 5.08mm (0.2") Pitch Standard Profile 90 ̊ Rising Clamp Terminal, 3 pole The real-life connectors are modular, made up of two or three connector blocks slotted together. These can be further slotted together to make larger connectors. Fritzing part is derived from Screw terminals by Lionel Michel. Because of the offset between connection pins and screw terminals, these are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
